# Fritzing sketch Balkong Relay plus temp and humitidy (saved by Fritzing 0.9.3b)
perfboards: 1

parts:
  R1 = Resistor [tolerance=±5% resistance=220 package=THT]
  WeMos_D1_Mini1 = WeMos D1 Mini  # not connected
  WeMos_D1_Mini_Relay_Shield_V1 = WeMos D1 Mini Relay Shield V2
  DHT1 = DHT11 Humitidy and Temperature Sensor
  Part1 = DC-DC Power Module (5v)  # not connected
  LED2 = smd LED [color="Red (633nm)" package="1206 [SMD]"]  # not connected
  LED3 = LEDs [package=led10mm]

nets:
  N1: R1.Pin_1, WeMos_D1_Mini_Relay_Shield_V1.D7
  N2: WeMos_D1_Mini_Relay_Shield_V1.D8, DHT1.VDD
  N3: WeMos_D1_Mini_Relay_Shield_V1.NO, LED3.C

custom parts:
  DHT11 Humitidy and Temperature Sensor: DHT11 Humidity and Temperature Sensor
  DC-DC Power Module (5v): DC-DC Power Module based con AMS1117-5.0 Input: DC 6~12V (input power must higher 1V than output power); Output: 5V (+/-0.05V error), 800mA
  LEDs: LEDs Standard schematic elements and footprints for 5mm, 3mm, 1206, and 0603 sized LEDs. 5mm - Spark Fun Electronics SKU : COM-00529 (and others)
