# Fritzing sketch Door Sensor (saved by Fritzing 0.9.3b)
perfboards: 1

parts:
  WeMos_D1_Mini_Relay_Shield_V1 = WeMos D1 Mini Relay Shield V2
  Part1 = DC-DC Power Module (5v)  # not connected
  LED3 = LEDs [package=led10mm]
  Part2 = Arduino Pro Mini (5V)
  R1 = Photocell (LDR) [package=THT]

nets:
  N1: WeMos_D1_Mini_Relay_Shield_V1.D0, Part2.D2
  N2: WeMos_D1_Mini_Relay_Shield_V1.NO, LED3.C
  N3: Part2.D4, R1.pin_0

custom parts:
  DC-DC Power Module (5v): DC-DC Power Module based con AMS1117-5.0 Input: DC 6~12V (input power must higher 1V than output power); Output: 5V (+/-0.05V error), 800mA
